# Fritzing sketch slider (saved by Fritzing 0.9.4)
circuit board: 8.46667cm x 5.64444cm
breadboards: 1

parts:
  Voltage_regulator = RioRand LM2596
  Stepper_Driver = L293D [package=THT]
  Stepper = Stepper Motor - Bipolar
  Arduino = Arduino Nano (Rev3.0)
  Bluetooth_Module = Bluetooth HC-05 Macho
  Battery_Terminals = Screw terminal - 2 pins [package=THT]
  Limit_Switch_1 = Toggle Switch [package=THT]
  Limit_Switch_2 = Toggle Switch [package=THT]

nets:
  N1: Voltage_regulator.Pin_1, Stepper_Driver.+Vmotor, Battery_Terminals.pin2
  N2: Voltage_regulator.Pin_2, Battery_Terminals.pin1
  VIN: Voltage_regulator.Pin_3, Stepper_Driver.Enable_1, Stepper_Driver.Enable_2, Stepper_Driver.+V, Arduino.VIN, Bluetooth_Module.VCC
  GND: Voltage_regulator.Pin_4, Stepper_Driver.0V, Arduino.GND, Bluetooth_Module.GND, Limit_Switch_1.COM, Limit_Switch_2.COM
  N3: Stepper_Driver.In_1, Arduino.D9
  N4: Stepper_Driver.Out_1_(_Controlled_by_Enable_1_), Stepper.A
  N5: Stepper_Driver.Out_2_(_Controlled_by_Enable_1_), Stepper.B
  N6: Stepper_Driver.In_2, Arduino.D10
  N7: Stepper_Driver.In_3, Arduino.D11/MOSI
  N8: Stepper_Driver.Out_3_(_Controlled_by_Enable_2_), Stepper.D
  N9: Stepper_Driver.Out_4_(_Controlled_by_Enable_2_), Stepper.C
  N10: Stepper_Driver.In_4, Arduino.D12/MISO
  N11: Arduino.D1/TX, Bluetooth_Module.RXD
  N12: Arduino.D0/RX, Bluetooth_Module.TXD
  N13: Arduino.D2, Limit_Switch_1.L2
  N14: Arduino.D3, Limit_Switch_2.L2
